# Fritzing sketch Stepper Circuit Diagram (saved by Fritzing 0.9.9b)
breadboards: 1

parts:
  Part1 = Arduino Uno (Rev3)
  Power_plug1 = Power plug
  C1 = Electrolytic Capacitor [capacitance=100µF voltage=35V package="200 mil [THT, electrolytic]"]
  M1 = Stepper Motor - Bipolar
  DRV_1 = Pololu A4988 [package=SO16]

nets:
  N1: Part1.D2, DRV_1.DIR
  N2: Part1.D3_PWM, DRV_1.STEP
  N3: Part1.5V, DRV_1.RESET, DRV_1.SLEEP
  N4: Part1.GND, DRV_1.GND#8
  N5: Power_plug1.GND, C1.-, DRV_1.GND#14
  N6: Power_plug1.VCC, C1.+, DRV_1.VMOT
  N7: M1.A, DRV_1.2B
  N8: M1.C, DRV_1.2A
  N9: M1.B, DRV_1.1A
  N10: M1.D, DRV_1.1B
